# Fritzing sketch safety-beacon (saved by Fritzing 0.9.9b)
breadboards: 1

parts:
  R1 = Resistor [tolerance=±5% power=0.25 resistance=100 package=THT]
  RED_LED = LED - 5mm [color="Red (633nm)" current=0.030 package="5 mm [THT]"]

nets:
  N1: R1.Pin_1, RED_LED.cathode
